# Fritzing sketch sketch (saved by Fritzing 0.9.5d)
breadboards: 1

parts:
  MCU1 = Raspberry Pi Zero
  LED1 = RGB LED (com. anode, rbg) [package="5 mm [THT]"]
  R1 = Resistor [tolerance=±5% resistance=220 package="0402 [SMD]"]
  R2 = Resistor [tolerance=±5% resistance=220 package="0402 [SMD]"]
  R3 = Resistor [tolerance=±5% resistance=220 package="0402 [SMD]"]
  S1 = Pushbutton [package="[THT]"]
  R4 = Resistor [tolerance=±5% resistance=220 package="0402 [SMD]"]

nets:
  N1: MCU1.pin_1, LED1.common_anode, R4.Pin_0
  N2: MCU1.pin_8, R3.Pin_1
  N3: MCU1.pin_10, R2.Pin_1
  N4: MCU1.pin_38, S1.Pin_1, S1.Pin_2
  N5: MCU1.pin_40, R1.Pin_0
  N6: LED1.red_cathode, R1.Pin_1
  N7: LED1.blue_cathode, R2.Pin_0
  N8: LED1.green_cathode, R3.Pin_0
  N9: S1.Pin_3, S1.Pin_4, R4.Pin_1
